# Fritzing sketch DipSwitch Platine (saved by Fritzing 0.9.3b)
stripboards: 1

parts:
  DipSwitch = DIP Switch 8 Position [package=dipswitch-08]
  R1 = Resistor [tolerance=±1% resistance=10k package=THT]
  R2 = Resistor [tolerance=±1% resistance=1k package=THT]
  R3 = Resistor [tolerance=±1% resistance=5.1k package=THT]
  R4 = Resistor [tolerance=±1% resistance=20k package=THT]
  eitech_robotics1 = eitech robotics

nets:
  N1: DipSwitch.1, R4.Pin_1
  N2: DipSwitch.2, R3.Pin_1
  N3: DipSwitch.3, R2.Pin_1
  N4: DipSwitch.14, DipSwitch.15, DipSwitch.16, R1.Pin_1, eitech_robotics1.IO_J7
  N5: R1.Pin_0, eitech_robotics1.5V_J7
  N6: R2.Pin_0, R3.Pin_0, R4.Pin_0, eitech_robotics1.GND_J7

custom parts:
  eitech robotics: Arduino Platine von Mattias Schlenker in Kooperation mit dem TÖP Rabutz
